// Digital circuit Memory Devices.dig as structural Verilog
module Memory_Devices (
  input  Address,
  input  Data_In,
  input  Read,
  input  Write,
  input  [2:0] Device_Select,
  input  Debug_Data,
  input  Exec_Clock,
  input  RAM_Clock,
  input  SPI_Clock,
  input  _10khz_Clock,
  input  Debug_Enable,
  input  SPI_CIDO,
  input  RAM_Bus_In,
  output Data_Out,
  output Ready,
  output Instruction_Cache_Clear,
  output Data_Cache_Clear,
  output SPI_IRQ,
  output SPI_CLK,
  output SPI_CODI,
  output SPI_CD,
  output SPI_SEL,
  output RAM_Bus_Out,
  output RAM_Bus_OE,
  output RAM_ALE,
  output RAM_AHE,
  output RAM_RE,
  output RAM_WE
);

  wire bootrom_1_data, bootrom_1_ready, debug_controller_1_spi_address, debug_controller_1_spi_data_out,
       debug_controller_1_spi_read, debug_controller_1_spi_write, demultiplexer_1_out_0,
       demultiplexer_1_out_1, demultiplexer_1_out_2, demultiplexer_1_out_3, demultiplexer_2_out_0,
       demultiplexer_2_out_1, demultiplexer_2_out_2, demultiplexer_2_out_3, multiplexer_1_out,
       multiplexer_2_out, multiplexer_3_out, multiplexer_4_out, ram_interface_1_data_out,
       ram_interface_1_ready, spi_interface_1_data_out;

  Demultiplexer #(.Selector_Bits(3)) demultiplexer_1 (
    .sel(Device_Select), .in(Write), .out_0(demultiplexer_1_out_0), .out_1(demultiplexer_1_out_1),
    .out_2(demultiplexer_1_out_2), .out_3(demultiplexer_1_out_3));  // open: out_4, out_5, out_6, out_7
  // NotConnected on demultiplexer_1_out_0
  Demultiplexer #(.Selector_Bits(3)) demultiplexer_2 (
    .sel(Device_Select), .in(Read), .out_0(demultiplexer_2_out_0), .out_1(demultiplexer_2_out_1),
    .out_2(demultiplexer_2_out_2), .out_3(demultiplexer_2_out_3));  // open: out_4, out_5, out_6, out_7
  // NotConnected on demultiplexer_2_out_1
  Bootrom bootrom_1 (.Address(Address), .Read(demultiplexer_2_out_0), .Data(bootrom_1_data), .Ready(bootrom_1_ready));
  Cache_Controller cache_controller_1 (
    .Address(Address), .Write(demultiplexer_1_out_1), .CLK(Exec_Clock),
    .Insutrction_Cache_Clear(Instruction_Cache_Clear), .Data_Cache_Clear(Data_Cache_Clear));
  RAM_Interface ram_interface_1 (
    .Address(Address), .Data_In(Data_In), .Read_In(demultiplexer_2_out_3), .Write_In(demultiplexer_1_out_3),
    .Exec_Clock(Exec_Clock), .RAM_Clock(RAM_Clock), .Bus_In(RAM_Bus_In), .Data_Out(ram_interface_1_data_out),
    .Ready(ram_interface_1_ready), .Bus_Out(RAM_Bus_Out), .Bus_OE(RAM_Bus_OE), .ALE(RAM_ALE), .AHE(RAM_AHE),
    .RE(RAM_RE), .WE(RAM_WE));
  Debug_Controller debug_controller_1 (
    .Debug_Data(Debug_Data), .SPI_Data_In(spi_interface_1_data_out), .Enable(Debug_Enable),
    .Exec_Clock(Exec_Clock), .RAM_Clock(RAM_Clock), .SPI_Clock(SPI_Clock),
    .SPI_Address(debug_controller_1_spi_address), .SPI_Data_Out(debug_controller_1_spi_data_out),
    .SPI_Read(debug_controller_1_spi_read), .SPI_Write(debug_controller_1_spi_write));
  Multiplexer multiplexer_1 (
    .sel(Debug_Enable), .in_0(Address), .in_1(debug_controller_1_spi_address), .out(multiplexer_1_out));
  Multiplexer multiplexer_2 (
    .sel(Debug_Enable), .in_0(Data_In), .in_1(debug_controller_1_spi_data_out), .out(multiplexer_2_out));
  Multiplexer multiplexer_3 (
    .sel(Debug_Enable), .in_0(demultiplexer_2_out_2), .in_1(debug_controller_1_spi_read),
    .out(multiplexer_3_out));
  Multiplexer multiplexer_4 (
    .sel(Debug_Enable), .in_0(demultiplexer_1_out_2), .in_1(debug_controller_1_spi_write),
    .out(multiplexer_4_out));
  SPI_Interface spi_interface_1 (
    .Address(multiplexer_1_out), .Data_In(multiplexer_2_out), .Read(multiplexer_3_out),
    .Write(multiplexer_4_out), .Exec_Clock(Exec_Clock), .SPI_Clock(SPI_Clock), .CIDO(SPI_CIDO),
    .Data_Out(spi_interface_1_data_out), .Interrupt(SPI_IRQ), .CLK(SPI_CLK), .CODI(SPI_CODI), .CD(SPI_CD),
    .SEL(SPI_SEL));
  Multiplexer #(.Selector_Bits(3)) multiplexer_5 (
    .sel(Device_Select), .in_0(bootrom_1_data), .in_1(1'b0), .in_2(spi_interface_1_data_out),
    .in_3(ram_interface_1_data_out), .out(Data_Out));  // open: in_4, in_5, in_6, in_7
  Multiplexer #(.Selector_Bits(3)) multiplexer_6 (
    .sel(Device_Select), .in_0(bootrom_1_ready), .in_1(1'b1), .in_2(1'b1), .in_3(ram_interface_1_ready),
    .out(Ready));  // open: in_4, in_5, in_6, in_7
  // Pins of 1 and 3 bits meet at Device_Select

  // Notes on the sheet:
  //   Internal
  //   Interface
endmodule
