// Digital circuit NST Chip.dig as structural Verilog
module NST_Chip (
  input  Memory_Bus_IN,
  input  SPI_CIDO,
  input  Keypad_Data,
  input  BTN_1,
  input  BTN_2,
  input  Device_Exec_Clock,
  input  Device_RAM_Clock,
  input  Device_SPI_Clock,
  input  Device_10KHz_Clock,
  output Memory_Bus_OUT,
  output Memory_Bus_OE,
  output M_Addr__Low_Clock,
  output M_Addr__High_Clock,
  output Memory_Read,
  output Memory_Write,
  output SPI_CLK,
  output SPI_CODI,
  output SPI_CD,
  output SPI_SEL,
  output Keypad_Select,
  output LEDs
);

  wire dcache_1_mem_address, dcache_1_mem_data_out, dcache_1_mem_read, dcache_1_mem_write,
       dcache_1_request_data_out, dcache_1_request_ready, icache_1_address_out, icache_1_read,
       memory_controller_1_dcache_address_out, memory_controller_1_dcache_data_out,
       memory_controller_1_dcache_read_out, memory_controller_1_dcache_ready_out,
       memory_controller_1_dcache_request_data_out, memory_controller_1_dcache_write_out,
       memory_controller_1_device_address, memory_controller_1_device_data_out,
       memory_controller_1_device_read, memory_controller_1_device_select, memory_controller_1_device_write,
       memory_controller_1_icache_data, memory_controller_1_icache_ready, memory_devices_1_data_cache_clear,
       memory_devices_1_data_out, memory_devices_1_instruction_cache_clear, memory_devices_1_ready;

  Memory_Controller memory_controller_1 (
    .ICache_Address(icache_1_address_out), .ICache_Read(icache_1_read),
    .DCache_Address_In(dcache_1_mem_address), .DCache_Request_Data_In(dcache_1_request_data_out),
    .DCache_Data_In(dcache_1_mem_data_out), .DCache_Read_In(dcache_1_mem_read),
    .DCache_Write_In(dcache_1_mem_write), .DCache_Ready_In(dcache_1_request_ready),
    .Device_Data_In(memory_devices_1_data_out), .Device_Ready(memory_devices_1_ready),
    .CLK(Device_Exec_Clock), .ICache_Data(memory_controller_1_icache_data),
    .ICache_Ready(memory_controller_1_icache_ready),
    .DCache_Address_Out(memory_controller_1_dcache_address_out),
    .DCache_Request_Data_Out(memory_controller_1_dcache_request_data_out),
    .DCache_Data_Out(memory_controller_1_dcache_data_out),
    .DCache_Read_Out(memory_controller_1_dcache_read_out),
    .DCache_Write_Out(memory_controller_1_dcache_write_out),
    .DCache_Ready_Out(memory_controller_1_dcache_ready_out),
    .Device_Address(memory_controller_1_device_address),
    .Device_Data_Out(memory_controller_1_device_data_out), .Device_Read(memory_controller_1_device_read),
    .Device_Write(memory_controller_1_device_write), .Device_Select(memory_controller_1_device_select));  // open: Exec_Address, Exec_Data_In, Exec_Read, Exec_Write, Exec_Data_Out, Exec_Ready
  Memory_Devices memory_devices_1 (
    .Address(memory_controller_1_device_address), .Data_In(memory_controller_1_device_data_out),
    .Read(memory_controller_1_device_read), .Write(memory_controller_1_device_write),
    .Device_Select(memory_controller_1_device_select), .Exec_Clock(Device_Exec_Clock),
    .RAM_Clock(Device_RAM_Clock), .SPI_Clock(Device_SPI_Clock), ._10khz_Clock(Device_10KHz_Clock),
    .SPI_CIDO(SPI_CIDO), .RAM_Bus_In(Memory_Bus_IN), .Data_Out(memory_devices_1_data_out),
    .Ready(memory_devices_1_ready), .Instruction_Cache_Clear(memory_devices_1_instruction_cache_clear),
    .Data_Cache_Clear(memory_devices_1_data_cache_clear), .SPI_CLK(SPI_CLK), .SPI_CODI(SPI_CODI),
    .SPI_CD(SPI_CD), .SPI_SEL(SPI_SEL), .RAM_Bus_Out(Memory_Bus_OUT), .RAM_Bus_OE(Memory_Bus_OE),
    .RAM_ALE(M_Addr__Low_Clock), .RAM_AHE(M_Addr__High_Clock), .RAM_RE(Memory_Read), .RAM_WE(Memory_Write));  // open: Debug_Data, Debug_Enable, SPI_IRQ
  ICache icache_1 (
    .Data_In(memory_controller_1_icache_data), .Ready_In(memory_controller_1_icache_ready),
    .Clear(memory_devices_1_instruction_cache_clear), .CLK(Device_Exec_Clock),
    .Address_Out(icache_1_address_out), .Read(icache_1_read));  // open: Address_In, Data_Out, Ready_Out
  DCache dcache_1 (
    .Request_Address(memory_controller_1_dcache_address_out),
    .Request_Data_In(memory_controller_1_dcache_request_data_out),
    .Request_Read(memory_controller_1_dcache_read_out), .Request_Write(memory_controller_1_dcache_write_out),
    .Mem_Data_In(memory_controller_1_dcache_data_out), .Mem_Ready(memory_controller_1_dcache_ready_out),
    .Clear(memory_devices_1_data_cache_clear), .CLK(Device_Exec_Clock),
    .Request_Data_Out(dcache_1_request_data_out), .Request_Ready(dcache_1_request_ready),
    .Mem_Address(dcache_1_mem_address), .Mem_Data_Out(dcache_1_mem_data_out), .Mem_Read(dcache_1_mem_read),
    .Mem_Write(dcache_1_mem_write));

  // Notes on the sheet:
  //   Arrows indicate flow of data, but not control
  //   Data Cache
  //   Processor
  //   Memory Controller
  //   Memory Devices
  //   Instruction Cache
endmodule
