// Digital circuit Handheld Board.dig as structural Verilog
module Handheld_Board (
  input  clk,
  input  clk_2,
  input  clk_3,
  input  clk_4
);

  wire button_1_out, button_2_out, demultiplexer_1_out_0, demultiplexer_1_out_1, demultiplexer_1_out_2,
       demultiplexer_1_out_3, demultiplexer_1_out_7, driver_1_out, notconnected_3_out, notconnected_4_out,
       notconnected_5_out, nst_chip_1_p1, nst_chip_1_p2, nst_chip_1_p3, nst_chip_1_p10, nst_chip_1_p11,
       nst_chip_1_p12, nst_chip_1_p13, nst_chip_1_p14, nst_chip_1_p15, nst_chip_1_p17, nst_chip_1_p18,
       nst_chip_1_p19, nst_chip_1_p20;
  wire [2:0] nst_chip_1_p16;
  wire [3:0] nst_chip_1_p21;

  Button button_1 (.out(button_1_out));
  Button button_2 (.out(button_2_out));
  // NST_Chip nst_chip_1: pin names not known; wires that end beside it: nst_chip_1_p1, nst_chip_1_p2, nst_chip_1_p3, button_1_out, button_2_out, clk, clk_2, clk_3, clk_4, nst_chip_1_p10, nst_chip_1_p11, nst_chip_1_p12, nst_chip_1_p13, nst_chip_1_p14, nst_chip_1_p15, nst_chip_1_p16, nst_chip_1_p17, nst_chip_1_p18, nst_chip_1_p19, nst_chip_1_p20, nst_chip_1_p21
  // NotConnected on nst_chip_1_p3
  // NotConnected on nst_chip_1_p20
  LED led_1 (.in(nst_chip_1_p21[0]));
  LED led_2 (.in(nst_chip_1_p21[1]));
  LED led_3 (.in(nst_chip_1_p21[2]));
  LED led_4 (.in(nst_chip_1_p21[3]));
  // NotConnected on notconnected_3_out
  // NotConnected on notconnected_4_out
  // NotConnected on notconnected_5_out
  assign driver_1_out = nst_chip_1_p11 ? nst_chip_1_p10 : 1'bz;  // Driver driver_1
  assign nst_chip_1_p1 = ~nst_chip_1_p11 ? driver_1_out : 1'bz;  // DriverInvSel driverinvsel_1
  Demultiplexer #(.Default(1), .Selector_Bits(3)) demultiplexer_1 (
    .sel(nst_chip_1_p16), .in(1'b0), .out_0(demultiplexer_1_out_0), .out_1(demultiplexer_1_out_1),
    .out_2(demultiplexer_1_out_2), .out_3(demultiplexer_1_out_3), .out_4(notconnected_4_out),
    .out_5(notconnected_5_out), .out_6(notconnected_3_out), .out_7(demultiplexer_1_out_7));
  // NotConnected on demultiplexer_1_out_0
  Board_ILI9341 board_ili9341_1 (
    .CLK(nst_chip_1_p17), .CODI(nst_chip_1_p18), .CD(nst_chip_1_p19), .CS(demultiplexer_1_out_1),
    .SD_CS(demultiplexer_1_out_2), .CIDO(nst_chip_1_p2));
  LCD lcd_1 (.CLK(nst_chip_1_p17), .CODI(nst_chip_1_p18), .CD(nst_chip_1_p19), .CS(demultiplexer_1_out_3));
  Debugger debugger_1 (
    .CLK(nst_chip_1_p17), .CODI(nst_chip_1_p18), .CD(nst_chip_1_p19), .CS(demultiplexer_1_out_7),
    .CIDO(nst_chip_1_p2));
  Board_Memory_Subsystem board_memory_subsystem_1 (
    .Address_Low_Clock(nst_chip_1_p12), .Address_High_Clock(nst_chip_1_p13), .OE(nst_chip_1_p14),
    .WE(nst_chip_1_p15), .Memory_Bus(driver_1_out));

  // Notes on the sheet:
  //   SPI Bus
endmodule
